# Fritzing sketch buttonControlCircuit (saved by Fritzing 0.9.1b)
circuit board: 8.46667cm x 5.64444cm
breadboards: 1

parts:
  Part1 = Arduino Uno (Rev3)
  S1 = Pushbutton [package="[THT]"]
  S2 = Pushbutton [package="[THT]"]
  J1 = Basic Servo
  R4 = Resistor [tolerance=±5% resistance=10k package=THT]
  R5 = Resistor [tolerance=±5% resistance=10k package=THT]

nets:
  N1: Part1.A1, S2.Pin_3, S2.Pin_4, R5.Pin_1
  N2: Part1.A2, S1.Pin_3, S1.Pin_4, R4.Pin_0
  N3: Part1.D9_PWM, J1.pulse
  GND: Part1.GND, S1.Pin_1, S1.Pin_2, S2.Pin_1, S2.Pin_2, J1.gnd
  5V: Part1.5V, J1.vcc, R4.Pin_1, R5.Pin_0
